// Logisim project LC-2200-16.circ as structural Verilog: 6 circuits, main circuit LC2200 Datapath
module LC2200_Datapath (
);

  wire CanReadGraphicsData, CLK, comparator_1_eq, DrALU, DrMEM, DrOFF, DrPC, DrREG, LdA, LdB, LdIR, LdMAR,
       LdPC, LdZ, RESET, WrMEM, WrREG, Z;
  wire [1:0] func, microcontroller_1_regsello;
  wire [2:0] OP;
  wire [3:0] bit_extender_1_out, bit_extender_2_out, controlled_buffer_1_out, controlled_buffer_1_out_2,
       regno, RX, RY;
  wire [4:0] OFFSET;
  wire [15:0] A_q, alu_1_out, B_q, bit_extender_3_out, CurrGraphicsAddress, GraphicsData, MAR_q, PC_q,
       ram_1_dout, Registers_dout, v0;
  wire [15:8] controlled_buffer_1_out_3;
  wire [31:0] graphics_controller_1_row1, graphics_controller_1_row2, graphics_controller_1_row3,
       graphics_controller_1_row4, graphics_controller_1_row5, graphics_controller_1_row6,
       graphics_controller_1_row7, graphics_controller_1_row8, graphics_controller_1_row9,
       graphics_controller_1_row10, graphics_controller_1_row11, graphics_controller_1_row12,
       graphics_controller_1_row13, graphics_controller_1_row14, graphics_controller_1_row15,
       graphics_controller_1_row16, graphics_controller_1_row17, graphics_controller_1_row18,
       graphics_controller_1_row19, graphics_controller_1_row20, graphics_controller_1_row21,
       graphics_controller_1_row22, graphics_controller_1_row23, graphics_controller_1_row24,
       graphics_controller_1_row25, graphics_controller_1_row26, graphics_controller_1_row27,
       graphics_controller_1_row28, graphics_controller_1_row29, graphics_controller_1_row30,
       graphics_controller_1_row31, graphics_controller_1_row32;

  Hex_Digit_Display hex_digit_display_1 (.value(controlled_buffer_1_out_3[15:12]));  // open: dp
  Hex_Digit_Display hex_digit_display_2 (.value(v0[15:12]));  // open: dp
  Hex_Digit_Display hex_digit_display_3 (.value(controlled_buffer_1_out_3[11:8]));  // open: dp
  Hex_Digit_Display hex_digit_display_4 (.value(controlled_buffer_1_out_2));  // open: dp
  Hex_Digit_Display hex_digit_display_5 (.value(v0[11:8]));  // open: dp
  Button u_RESET (.out(RESET));
  Clock u_CLK (.out(CLK));
  Hex_Digit_Display hex_digit_display_6 (.value(controlled_buffer_1_out));  // open: dp
  Comparator #(.width(16), .mode("unsigned")) comparator_1 (
    .a({controlled_buffer_1_out_3, controlled_buffer_1_out_2, controlled_buffer_1_out}), .b({16{1'b0}}),
    .eq(comparator_1_eq));  // open: gt, lt
  Hex_Digit_Display hex_digit_display_7 (.value(v0[7:4]));  // open: dp
  Hex_Digit_Display hex_digit_display_8 (.value(v0[3:0]));  // open: dp
  assign bit_extender_1_out = {{1{1'b0}}, OP};  // Bit_Extender bit_extender_1
  Register #(.width(16)) PC (
    .D({controlled_buffer_1_out_3, controlled_buffer_1_out_2, controlled_buffer_1_out}), .en(LdPC), .Q(PC_q),
    .clk(CLK), .clr(RESET));
  assign {controlled_buffer_1_out_3, controlled_buffer_1_out_2, controlled_buffer_1_out} = DrPC ? PC_q : 16'bz;  // Controlled_Buffer controlled_buffer_1
  Register #(.width(1)) u_Z (.D(comparator_1_eq), .en(LdZ), .Q(Z), .clk(CLK));  // open: clr
  Hex_Digit_Display hex_digit_display_9 (.value(bit_extender_1_out));  // open: dp
  Hex_Digit_Display hex_digit_display_10 (.value(RX));  // open: dp
  Register #(.width(16)) A (
    .D({controlled_buffer_1_out_3, controlled_buffer_1_out_2, controlled_buffer_1_out}), .en(LdA), .Q(A_q),
    .clk(CLK));  // open: clr
  Hex_Digit_Display hex_digit_display_11 (.value(RY));  // open: dp
  ALU alu_1 (.func(func), .A(A_q), .B(B_q), .OUT(alu_1_out));
  assign {controlled_buffer_1_out_3, controlled_buffer_1_out_2, controlled_buffer_1_out} = DrALU ? alu_1_out : 16'bz;  // Controlled_Buffer controlled_buffer_2
  Hex_Digit_Display hex_digit_display_12 (.value(OFFSET[4:1]));  // open: dp
  Register #(.width(16)) B (
    .D({controlled_buffer_1_out_3, controlled_buffer_1_out_2, controlled_buffer_1_out}), .en(LdB), .Q(B_q),
    .clk(CLK));  // open: clr
  Graphics_Controller graphics_controller_1 (
    .CLK(CLK), .RESET(RESET), .CanReadGraphicsData(CanReadGraphicsData), .Graphics_Memory_Address(16'hffc0),
    .CurrGraphicsAddress(CurrGraphicsAddress), .GraphicsData(GraphicsData),
    .Row1(graphics_controller_1_row1), .Row2(graphics_controller_1_row2), .Row3(graphics_controller_1_row3),
    .Row4(graphics_controller_1_row4), .Row5(graphics_controller_1_row5), .Row6(graphics_controller_1_row6),
    .Row7(graphics_controller_1_row7), .Row8(graphics_controller_1_row8), .Row9(graphics_controller_1_row9),
    .Row10(graphics_controller_1_row10), .Row11(graphics_controller_1_row11),
    .Row12(graphics_controller_1_row12), .Row13(graphics_controller_1_row13),
    .Row14(graphics_controller_1_row14), .Row15(graphics_controller_1_row15),
    .Row16(graphics_controller_1_row16), .Row17(graphics_controller_1_row17),
    .Row18(graphics_controller_1_row18), .Row19(graphics_controller_1_row19),
    .Row20(graphics_controller_1_row20), .Row21(graphics_controller_1_row21),
    .Row22(graphics_controller_1_row22), .Row23(graphics_controller_1_row23),
    .Row24(graphics_controller_1_row24), .Row25(graphics_controller_1_row25),
    .Row26(graphics_controller_1_row26), .Row27(graphics_controller_1_row27),
    .Row28(graphics_controller_1_row28), .Row29(graphics_controller_1_row29),
    .Row30(graphics_controller_1_row30), .Row31(graphics_controller_1_row31),
    .Row32(graphics_controller_1_row32));
  Hex_Digit_Display hex_digit_display_13 (.value(bit_extender_2_out));  // open: dp
  Hex_Digit_Display hex_digit_display_14 (.value(OFFSET[3:0]));  // open: dp
  assign {controlled_buffer_1_out_3, controlled_buffer_1_out_2, controlled_buffer_1_out} = DrREG ? Registers_dout : 16'bz;  // Controlled_Buffer controlled_buffer_3
  DotMatrix #(.inputtype("row"), .matrixcols(32), .matrixrows(32)) dotmatrix_1 (
    .row0(graphics_controller_1_row1), .row1(graphics_controller_1_row2), .row2(graphics_controller_1_row3),
    .row3(graphics_controller_1_row4), .row4(graphics_controller_1_row5), .row5(graphics_controller_1_row6),
    .row6(graphics_controller_1_row7), .row7(graphics_controller_1_row8), .row8(graphics_controller_1_row9),
    .row9(graphics_controller_1_row10), .row10(graphics_controller_1_row11),
    .row11(graphics_controller_1_row12), .row12(graphics_controller_1_row13),
    .row13(graphics_controller_1_row14), .row14(graphics_controller_1_row15),
    .row15(graphics_controller_1_row16), .row16(graphics_controller_1_row17),
    .row17(graphics_controller_1_row18), .row18(graphics_controller_1_row19),
    .row19(graphics_controller_1_row20), .row20(graphics_controller_1_row21),
    .row21(graphics_controller_1_row22), .row22(graphics_controller_1_row23),
    .row23(graphics_controller_1_row24), .row24(graphics_controller_1_row25),
    .row25(graphics_controller_1_row26), .row26(graphics_controller_1_row27),
    .row27(graphics_controller_1_row28), .row28(graphics_controller_1_row29),
    .row29(graphics_controller_1_row30), .row30(graphics_controller_1_row31),
    .row31(graphics_controller_1_row32));
  Registers Registers (
    .WrREG(WrREG), .regno(regno), .CLK(CLK), .v0(v0),
    .Din({controlled_buffer_1_out_3, controlled_buffer_1_out_2, controlled_buffer_1_out}),
    .Dout(Registers_dout));
  Register #(.width(16)) MAR (
    .D({controlled_buffer_1_out_3, controlled_buffer_1_out_2, controlled_buffer_1_out}), .en(LdMAR),
    .Q(MAR_q), .clk(CLK), .clr(RESET));
  assign bit_extender_2_out = {{3{1'b0}}, OFFSET[4]};  // Bit_Extender bit_extender_2
  RAM ram_1 (
    .WrMEM(WrMEM), .CLK(CLK), .SEGMENT_ADDRESS(16'hffc0), .CanReadGraphicsData(CanReadGraphicsData),
    .CurrGraphicsAddress(CurrGraphicsAddress), .GraphicsData(GraphicsData), .Addr(MAR_q),
    .Din({controlled_buffer_1_out_3, controlled_buffer_1_out_2, controlled_buffer_1_out}), .Dout(ram_1_dout),
    .DrMEM(DrMEM));
  assign {controlled_buffer_1_out_3, controlled_buffer_1_out_2, controlled_buffer_1_out} = DrMEM ? ram_1_dout : 16'bz;  // Controlled_Buffer controlled_buffer_4
  Register #(.width(16)) IR (
    .D({controlled_buffer_1_out_3, controlled_buffer_1_out_2, controlled_buffer_1_out}), .en(LdIR),
    .Q({OP, RX, RY, OFFSET}), .clk(CLK));  // open: clr
  assign bit_extender_3_out = {{11{OFFSET[4]}}, OFFSET};  // Bit_Extender bit_extender_3
  assign {controlled_buffer_1_out_3, controlled_buffer_1_out_2, controlled_buffer_1_out} = DrOFF ? bit_extender_3_out : 16'bz;  // Controlled_Buffer controlled_buffer_5
  Multiplexer #(.select(2), .width(4), .disabled(0), .enable("false")) multiplexer_1 (
    .in0(RX), .in1(RY), .in2(OFFSET[4:1]), .out(regno), .sel(microcontroller_1_regsello));  // open: in3
  Microcontroller microcontroller_1 (
    .LdMAR(LdMAR), .LdIR(LdIR), .LdPC(LdPC), .DrOFF(DrOFF), .DrPC(DrPC), .DrALU(DrALU), .DrMEM(DrMEM),
    .DrREG(DrREG), .LdA(LdA), .LdB(LdB), .LdZ(LdZ), .WrREG(WrREG), .WrMEM(WrMEM),
    .RegSelLo(microcontroller_1_regsello[0]), .RegSelHi(microcontroller_1_regsello[1]), .ALULo(func[0]),
    .ALUHi(func[1]), .IR(OP), .Z(Z), .RESET(RESET), .CLK(CLK));
  Hex_Digit_Display hex_digit_display_15 (.value(regno));  // open: dp

  // Other names for the same wires on the sheet: RZ[3:0] = OFFSET[4:1]

  // Notes on the sheet:
  //   BUS
  //   $v0
  //   OP
  //   RX
  //   RY
  //   RZ
  //   OFFSET
endmodule

module ALU (
  input  [15:0] A,
  input  [15:0] B,
  input  [1:0] func,
  output [15:0] OUT
);

  wire [15:0] ADD, NAND, plus_1, SUB;

  Adder #(.width(16)) adder_1 (.a(A), .b(B), .out(ADD));  // open: cin, cout
  Subtractor #(.width(16)) subtractor_1 (.a(A), .b(B), .out(SUB));  // open: bin, bout
  Multiplexer #(.select(2), .width(16), .disabled(0), .enable("false")) multiplexer_1 (
    .in0(ADD), .in1(NAND), .in2(SUB), .in3(plus_1), .out(OUT), .sel(func));
  assign NAND = ~(A & B);  // NAND_Gate nand_1, 16 bits wide
  Adder #(.width(16)) adder_2 (.a(A), .b(16'h1), .out(plus_1));  // open: cin, cout
endmodule

module Registers (
  input  [15:0] Din,
  input  WrREG,
  input  [3:0] regno,
  input  CLK,
  output [15:0] Dout,
  output [15:0] v0
);

  wire demultiplexer_1_out1, demultiplexer_1_out2, demultiplexer_1_out3, demultiplexer_1_out4,
       demultiplexer_1_out5, demultiplexer_1_out6, demultiplexer_1_out7, demultiplexer_1_out8,
       demultiplexer_1_out9, demultiplexer_1_out10, demultiplexer_1_out11, demultiplexer_1_out12,
       demultiplexer_1_out13, demultiplexer_1_out14, demultiplexer_1_out15;
  wire [15:0] _1____at_q, _3____a0_q, _4____a1_q, _5____a2_q, _6____t0_q, _7____t1_q, _8____t2_q, _9____s0_q,
       A____s1_q, B____s2_q, C____k0_q, D____sp_q, E____fp_q, F____ra_q;

  Demultiplexer #(.select(4), .disabled(0), .enable("false")) demultiplexer_1 (
    .out1(demultiplexer_1_out1), .out2(demultiplexer_1_out2), .out3(demultiplexer_1_out3),
    .out4(demultiplexer_1_out4), .out5(demultiplexer_1_out5), .out6(demultiplexer_1_out6),
    .out7(demultiplexer_1_out7), .out8(demultiplexer_1_out8), .out9(demultiplexer_1_out9),
    .out10(demultiplexer_1_out10), .out11(demultiplexer_1_out11), .out12(demultiplexer_1_out12),
    .out13(demultiplexer_1_out13), .out14(demultiplexer_1_out14), .out15(demultiplexer_1_out15), .in(WrREG),
    .sel(regno));  // open: out0
  Register #(.width(16)) _4____a1 (.D(Din), .en(demultiplexer_1_out4), .Q(_4____a1_q), .clk(CLK));  // open: clr
  Register #(.width(16)) _8____t2 (.D(Din), .en(demultiplexer_1_out8), .Q(_8____t2_q), .clk(CLK));  // open: clr
  Register #(.width(16)) C____k0 (.D(Din), .en(demultiplexer_1_out12), .Q(C____k0_q), .clk(CLK));  // open: clr
  Register #(.width(16)) _1____at (.D(Din), .en(demultiplexer_1_out1), .Q(_1____at_q), .clk(CLK));  // open: clr
  Register #(.width(16)) _5____a2 (.D(Din), .en(demultiplexer_1_out5), .Q(_5____a2_q), .clk(CLK));  // open: clr
  Register #(.width(16)) _9____s0 (.D(Din), .en(demultiplexer_1_out9), .Q(_9____s0_q), .clk(CLK));  // open: clr
  Register #(.width(16)) D____sp (.D(Din), .en(demultiplexer_1_out13), .Q(D____sp_q), .clk(CLK));  // open: clr
  Register #(.width(16)) _2____v0 (.D(Din), .en(demultiplexer_1_out2), .Q(v0), .clk(CLK));  // open: clr
  Register #(.width(16)) _6____t0 (.D(Din), .en(demultiplexer_1_out6), .Q(_6____t0_q), .clk(CLK));  // open: clr
  Register #(.width(16)) A____s1 (.D(Din), .en(demultiplexer_1_out10), .Q(A____s1_q), .clk(CLK));  // open: clr
  Register #(.width(16)) E____fp (.D(Din), .en(demultiplexer_1_out14), .Q(E____fp_q), .clk(CLK));  // open: clr
  Register #(.width(16)) _3____a0 (.D(Din), .en(demultiplexer_1_out3), .Q(_3____a0_q), .clk(CLK));  // open: clr
  Register #(.width(16)) _7____t1 (.D(Din), .en(demultiplexer_1_out7), .Q(_7____t1_q), .clk(CLK));  // open: clr
  Register #(.width(16)) B____s2 (.D(Din), .en(demultiplexer_1_out11), .Q(B____s2_q), .clk(CLK));  // open: clr
  Register #(.width(16)) F____ra (.D(Din), .en(demultiplexer_1_out15), .Q(F____ra_q), .clk(CLK));  // open: clr
  Multiplexer #(.select(4), .width(16), .disabled(0), .enable("false")) multiplexer_1 (
    .in0({16{1'b0}}), .in1(_1____at_q), .in2(v0), .in3(_3____a0_q), .in4(_4____a1_q), .in5(_5____a2_q),
    .in6(_6____t0_q), .in7(_7____t1_q), .in8(_8____t2_q), .in9(_9____s0_q), .in10(A____s1_q),
    .in11(B____s2_q), .in12(C____k0_q), .in13(D____sp_q), .in14(E____fp_q), .in15(F____ra_q), .out(Dout),
    .sel(regno));

  // Notes on the sheet:
  //   0 - $zero
endmodule

module RAM (
  input  [15:0] Din,
  input  [15:0] CurrGraphicsAddress,
  input  [15:0] Addr,
  input  WrMEM,
  input  CLK,
  input  [15:0] SEGMENT_ADDRESS,
  input  DrMEM,
  output CanReadGraphicsData,
  output [15:0] GraphicsData,
  output [15:0] Dout
);

  wire and_1_out, CLEAR_MEM1_out, comparator_1_gt, comparator_2_gt, demultiplexer_1_out1, not_1_out,
       not_2_out, or_1_out, or_2_out, WrMEM1, WrMEM2;
  wire [1:0] comparator_1_eq;
  wire [15:0] controlled_buffer_2_out, demultiplexer_2_out1, multiplexer_1_out, multiplexer_2_out,
       ram_1_data, ram_2_data, subtractor_1_out;

  Button CLEAR_MEM1 (.out(CLEAR_MEM1_out));
  Multiplexer #(.width(16), .disabled(0), .enable("false")) multiplexer_1 (
    .in0(Addr), .in1(CurrGraphicsAddress), .out(multiplexer_1_out), .sel(CanReadGraphicsData));
  Subtractor #(.width(16)) subtractor_1 (.a(SEGMENT_ADDRESS), .b(16'h1), .out(subtractor_1_out));  // open: bin, bout
  Comparator #(.width(16), .mode("unsigned")) comparator_1 (
    .a(Addr), .b(subtractor_1_out), .gt(comparator_1_gt), .eq(comparator_1_eq[0]), .lt(comparator_1_eq[1]));
  Comparator #(.width(16), .mode("unsigned")) comparator_2 (
    .a(CurrGraphicsAddress), .b(subtractor_1_out), .gt(comparator_2_gt));  // open: eq, lt
  RAM_part #(.addrWidth(16), .dataWidth(16)) ram_1 (
    .addr(multiplexer_1_out), .data(ram_1_data), .sel(1'b1), .clk(CLK), .ld(not_1_out), .clr(CLEAR_MEM1_out));
  not not_1 (not_1_out, WrMEM1);
  RAM_part #(.addrWidth(16), .dataWidth(16)) ram_2 (
    .addr(multiplexer_1_out), .data(ram_2_data), .sel(1'b1), .clk(CLK), .ld(not_2_out),
    .clr(demultiplexer_1_out1));
  not not_2 (not_2_out, WrMEM2);
  Demultiplexer #(.select(2), .disabled(0), .enable("false")) demultiplexer_1 (
    .out0(WrMEM2), .out1(demultiplexer_1_out1), .out2(WrMEM1), .in(WrMEM), .sel(comparator_1_eq));  // open: out3
  assign ram_2_data = WrMEM2 ? demultiplexer_2_out1 : 16'bz;  // Controlled_Buffer controlled_buffer_1
  assign controlled_buffer_2_out = WrMEM ? Din : 16'bz;  // Controlled_Buffer controlled_buffer_2
  Demultiplexer #(.width(16), .disabled(0), .enable("false")) demultiplexer_2 (
    .out0(ram_1_data), .out1(demultiplexer_2_out1), .in(controlled_buffer_2_out), .sel(comparator_1_gt));
  or or_1 (or_1_out, comparator_1_gt, and_1_out);
  Multiplexer #(.width(16), .disabled(0), .enable("false")) multiplexer_2 (
    .in0(ram_1_data), .in1(ram_2_data), .out(multiplexer_2_out), .sel(or_1_out));
  and and_1 (and_1_out, comparator_2_gt, CanReadGraphicsData);
  assign GraphicsData = CanReadGraphicsData ? multiplexer_2_out : 16'bz;  // Controlled_Buffer controlled_buffer_3
  assign Dout = DrMEM ? multiplexer_2_out : 16'bz;  // Controlled_Buffer controlled_buffer_4
  not not_3 (CanReadGraphicsData, or_2_out);
  or or_2 (or_2_out, WrMEM2, DrMEM);
endmodule

module Microcontroller (
  input  [2:0] IR,
  input  Z,
  input  RESET,
  input  CLK,
  output LdA,
  output LdB,
  output LdZ,
  output WrREG,
  output WrMEM,
  output RegSelLo,
  output RegSelHi,
  output ALULo,
  output ALUHi,
  output LdMAR,
  output LdIR,
  output LdPC,
  output DrOFF,
  output DrPC,
  output DrALU,
  output DrMEM,
  output DrREG
);

  wire chkZ;
  wire [5:0] multiplexer_1_out, rom_1_data, rom_2_data, State_q;
  wire [23:0] Microstate;

  ROM #(.addrWidth(3), .dataWidth(6)) rom_1 (.addr(IR), .data(rom_1_data), .sel(1'b1));
  ROM #(.addrWidth(2), .dataWidth(6)) rom_2 (.addr({1'b0, Z}), .data(rom_2_data), .sel(1'b1));
  Multiplexer #(.select(2), .width(6), .disabled(0), .enable("false")) multiplexer_1 (
    .in0(Microstate[5:0]), .in1(rom_1_data), .in2(rom_2_data), .out(multiplexer_1_out),
    .sel({chkZ, Microstate[23]}));  // open: in3
  Register #(.width(6)) State (.D(multiplexer_1_out), .en(1'b1), .Q(State_q), .clk(CLK), .clr(RESET));
  ROM #(.addrWidth(6), .dataWidth(25)) rom_3 (
    .addr(State_q),
    .data({chkZ, Microstate[23], ALUHi, ALULo, RegSelHi, RegSelLo, WrMEM, WrREG, LdZ, LdB, LdA, LdMAR, LdIR, LdPC, DrOFF, DrPC, DrALU, DrMEM, DrREG, Microstate[5:0]}),
    .sel(1'b1));

  // Other names for the same wires on the sheet: Microstate (some bits) = {chkZ, ALUHi, ALULo, RegSelHi, RegSelLo, WrMEM, WrREG, LdZ, LdB, LdA, LdMAR, LdIR, LdPC, DrOFF, DrPC, DrALU, DrMEM, DrREG};
  //   OPTest = Microstate[23]; Next_State[5:0] = Microstate[5:0]; OP[2:0] = IR

  // Notes on the sheet:
  //   contents of rom_1 (hex, n*v repeats v):
  //   3 9 6 c 10 14 1b 1d
  //   contents of rom_2 (hex, n*v repeats v):
  //   0 18
  //   contents of rom_3 (hex, n*v repeats v):
  //   6201 1082 e00900 84044 108045 20100 84047 8408 20100 8404a 10804b 220100 8404d 840e 210f 20080 84051
  //   8412 2113 40040 4055 88056 410117 1000000 4219 841a 900 a021c 840 1d
endmodule

module Graphics_Controller (
  input  CLK,
  input  RESET,
  input  CanReadGraphicsData,
  input  [15:0] Graphics_Memory_Address,
  input  [15:0] GraphicsData,
  output [31:0] Row1,
  output [31:0] Row2,
  output [31:0] Row3,
  output [31:0] Row4,
  output [31:0] Row5,
  output [31:0] Row6,
  output [31:0] Row7,
  output [31:0] Row8,
  output [31:0] Row9,
  output [31:0] Row10,
  output [31:0] Row11,
  output [31:0] Row12,
  output [31:0] Row13,
  output [31:0] Row14,
  output [31:0] Row15,
  output [31:0] Row16,
  output [31:0] Row17,
  output [31:0] Row18,
  output [31:0] Row19,
  output [31:0] Row20,
  output [31:0] Row21,
  output [31:0] Row22,
  output [31:0] Row23,
  output [31:0] Row24,
  output [31:0] Row25,
  output [31:0] Row26,
  output [15:0] CurrGraphicsAddress,
  output [31:0] Row27,
  output [31:0] Row28,
  output [31:0] Row29,
  output [31:0] Row30,
  output [31:0] Row31,
  output [31:0] Row32
);

  wire adder_2_cout;
  wire [5:0] adder_1_out, controlled_buffer_1_out, CurrReg_q;
  wire [15:0] bit_extender_1_out, demultiplexer_1_out0, demultiplexer_2_out0, demultiplexer_17_out0,
       demultiplexer_18_out0, demultiplexer_19_out0, demultiplexer_19_out16;

  Demultiplexer #(.disabled(0), .enable("false")) demultiplexer_1 (
    .out0(demultiplexer_1_out0[0]), .out1(demultiplexer_1_out0[1]), .in(demultiplexer_19_out0[0]),
    .sel(CurrReg_q[0]));
  Demultiplexer #(.disabled(0), .enable("false")) demultiplexer_2 (
    .out0(demultiplexer_2_out0[0]), .out1(demultiplexer_2_out0[1]), .in(demultiplexer_19_out16[0]),
    .sel(CurrReg_q[0]));
  Demultiplexer #(.disabled(0), .enable("false")) demultiplexer_3 (
    .out0(demultiplexer_1_out0[2]), .out1(demultiplexer_1_out0[3]), .in(demultiplexer_19_out0[1]),
    .sel(CurrReg_q[0]));
  Demultiplexer #(.disabled(0), .enable("false")) demultiplexer_4 (
    .out0(demultiplexer_2_out0[2]), .out1(demultiplexer_2_out0[3]), .in(demultiplexer_19_out16[1]),
    .sel(CurrReg_q[0]));
  Register #(.width(16)) register_1 (
    .D(GraphicsData), .en(demultiplexer_1_out0[0]), .Q(Row1[31:16]), .clk(CLK), .clr(RESET));
  Register #(.width(16)) register_2 (
    .D(GraphicsData), .en(demultiplexer_1_out0[1]), .Q(Row1[15:0]), .clk(CLK), .clr(RESET));
  Register #(.width(16)) register_3 (
    .D(GraphicsData), .en(demultiplexer_1_out0[2]), .Q(Row2[31:16]), .clk(CLK), .clr(RESET));
  Register #(.width(16)) register_4 (
    .D(GraphicsData), .en(demultiplexer_1_out0[3]), .Q(Row2[15:0]), .clk(CLK), .clr(RESET));
  Register #(.width(16)) register_5 (
    .D(GraphicsData), .en(demultiplexer_1_out0[4]), .Q(Row3[31:16]), .clk(CLK), .clr(RESET));
  Register #(.width(16)) register_6 (
    .D(GraphicsData), .en(demultiplexer_1_out0[5]), .Q(Row3[15:0]), .clk(CLK), .clr(RESET));
  Register #(.width(16)) register_7 (
    .D(GraphicsData), .en(demultiplexer_1_out0[6]), .Q(Row4[31:16]), .clk(CLK), .clr(RESET));
  Register #(.width(16)) register_8 (
    .D(GraphicsData), .en(demultiplexer_1_out0[7]), .Q(Row4[15:0]), .clk(CLK), .clr(RESET));
  Register #(.width(16)) register_9 (
    .D(GraphicsData), .en(demultiplexer_1_out0[8]), .Q(Row5[31:16]), .clk(CLK), .clr(RESET));
  Register #(.width(16)) register_10 (
    .D(GraphicsData), .en(demultiplexer_1_out0[9]), .Q(Row5[15:0]), .clk(CLK), .clr(RESET));
  Register #(.width(16)) register_11 (
    .D(GraphicsData), .en(demultiplexer_1_out0[10]), .Q(Row6[31:16]), .clk(CLK), .clr(RESET));
  Register #(.width(16)) register_12 (
    .D(GraphicsData), .en(demultiplexer_1_out0[11]), .Q(Row6[15:0]), .clk(CLK), .clr(RESET));
  Register #(.width(16)) register_13 (
    .D(GraphicsData), .en(demultiplexer_1_out0[12]), .Q(Row7[31:16]), .clk(CLK), .clr(RESET));
  Register #(.width(16)) register_14 (
    .D(GraphicsData), .en(demultiplexer_1_out0[13]), .Q(Row7[15:0]), .clk(CLK), .clr(RESET));
  Register #(.width(16)) register_15 (
    .D(GraphicsData), .en(demultiplexer_1_out0[14]), .Q(Row8[31:16]), .clk(CLK), .clr(RESET));
  Register #(.width(16)) register_16 (
    .D(GraphicsData), .en(demultiplexer_1_out0[15]), .Q(Row8[15:0]), .clk(CLK), .clr(RESET));
  Demultiplexer #(.disabled(0), .enable("false")) demultiplexer_5 (
    .out0(demultiplexer_1_out0[6]), .out1(demultiplexer_1_out0[7]), .in(demultiplexer_19_out0[3]),
    .sel(CurrReg_q[0]));
  Demultiplexer #(.disabled(0), .enable("false")) demultiplexer_6 (
    .out0(demultiplexer_1_out0[4]), .out1(demultiplexer_1_out0[5]), .in(demultiplexer_19_out0[2]),
    .sel(CurrReg_q[0]));
  Demultiplexer #(.disabled(0), .enable("false")) demultiplexer_7 (
    .out0(demultiplexer_2_out0[6]), .out1(demultiplexer_2_out0[7]), .in(demultiplexer_19_out16[3]),
    .sel(CurrReg_q[0]));
  Demultiplexer #(.disabled(0), .enable("false")) demultiplexer_8 (
    .out0(demultiplexer_2_out0[4]), .out1(demultiplexer_2_out0[5]), .in(demultiplexer_19_out16[2]),
    .sel(CurrReg_q[0]));
  Demultiplexer #(.disabled(0), .enable("false")) demultiplexer_9 (
    .out0(demultiplexer_1_out0[8]), .out1(demultiplexer_1_out0[9]), .in(demultiplexer_19_out0[4]),
    .sel(CurrReg_q[0]));
  Demultiplexer #(.disabled(0), .enable("false")) demultiplexer_10 (
    .out0(demultiplexer_2_out0[8]), .out1(demultiplexer_2_out0[9]), .in(demultiplexer_19_out16[4]),
    .sel(CurrReg_q[0]));
  Register #(.width(6)) CurrReg (.D(controlled_buffer_1_out), .Q(CurrReg_q), .clk(CLK), .clr(RESET));  // open: en
  assign controlled_buffer_1_out = CanReadGraphicsData ? adder_1_out : 6'bz;  // Controlled_Buffer controlled_buffer_1
  Demultiplexer #(.disabled(0), .enable("false")) demultiplexer_11 (
    .out0(demultiplexer_1_out0[10]), .out1(demultiplexer_1_out0[11]), .in(demultiplexer_19_out0[5]),
    .sel(CurrReg_q[0]));
  Demultiplexer #(.disabled(0), .enable("false")) demultiplexer_12 (
    .out0(demultiplexer_2_out0[10]), .out1(demultiplexer_2_out0[11]), .in(demultiplexer_19_out16[5]),
    .sel(CurrReg_q[0]));
  Adder #(.width(6)) adder_1 (.a(CurrReg_q), .b(6'b000001), .out(adder_1_out));  // open: cin, cout
  assign bit_extender_1_out = {{10{1'b0}}, CurrReg_q};  // Bit_Extender bit_extender_1
  Demultiplexer #(.disabled(0), .enable("false")) demultiplexer_13 (
    .out0(demultiplexer_1_out0[12]), .out1(demultiplexer_1_out0[13]), .in(demultiplexer_19_out0[6]),
    .sel(CurrReg_q[0]));
  Demultiplexer #(.disabled(0), .enable("false")) demultiplexer_14 (
    .out0(demultiplexer_1_out0[14]), .out1(demultiplexer_1_out0[15]), .in(demultiplexer_19_out0[7]),
    .sel(CurrReg_q[0]));
  Demultiplexer #(.disabled(0), .enable("false")) demultiplexer_15 (
    .out0(demultiplexer_2_out0[14]), .out1(demultiplexer_2_out0[15]), .in(demultiplexer_19_out16[7]),
    .sel(CurrReg_q[0]));
  Demultiplexer #(.disabled(0), .enable("false")) demultiplexer_16 (
    .out0(demultiplexer_2_out0[12]), .out1(demultiplexer_2_out0[13]), .in(demultiplexer_19_out16[6]),
    .sel(CurrReg_q[0]));
  Adder #(.width(16)) adder_2 (
    .a(bit_extender_1_out), .b(Graphics_Memory_Address), .out(CurrGraphicsAddress), .cout(adder_2_cout));  // open: cin
  // Probe on adder_2_cout
  Register #(.width(16)) register_17 (
    .D(GraphicsData), .en(demultiplexer_17_out0[0]), .Q(Row9[31:16]), .clk(CLK), .clr(RESET));
  Register #(.width(16)) register_18 (
    .D(GraphicsData), .en(demultiplexer_17_out0[1]), .Q(Row9[15:0]), .clk(CLK), .clr(RESET));
  Register #(.width(16)) register_19 (
    .D(GraphicsData), .en(demultiplexer_17_out0[2]), .Q(Row10[31:16]), .clk(CLK), .clr(RESET));
  Register #(.width(16)) register_20 (
    .D(GraphicsData), .en(demultiplexer_17_out0[3]), .Q(Row10[15:0]), .clk(CLK), .clr(RESET));
  Register #(.width(16)) register_21 (
    .D(GraphicsData), .en(demultiplexer_17_out0[4]), .Q(Row11[31:16]), .clk(CLK), .clr(RESET));
  Register #(.width(16)) register_22 (
    .D(GraphicsData), .en(demultiplexer_17_out0[5]), .Q(Row11[15:0]), .clk(CLK), .clr(RESET));
  Register #(.width(16)) register_23 (
    .D(GraphicsData), .en(demultiplexer_17_out0[6]), .Q(Row12[31:16]), .clk(CLK), .clr(RESET));
  Register #(.width(16)) register_24 (
    .D(GraphicsData), .en(demultiplexer_17_out0[7]), .Q(Row12[15:0]), .clk(CLK), .clr(RESET));
  Register #(.width(16)) register_25 (
    .D(GraphicsData), .en(demultiplexer_17_out0[8]), .Q(Row13[31:16]), .clk(CLK), .clr(RESET));
  Register #(.width(16)) register_26 (
    .D(GraphicsData), .en(demultiplexer_17_out0[9]), .Q(Row13[15:0]), .clk(CLK), .clr(RESET));
  Register #(.width(16)) register_27 (
    .D(GraphicsData), .en(demultiplexer_17_out0[10]), .Q(Row14[31:16]), .clk(CLK), .clr(RESET));
  Register #(.width(16)) register_28 (
    .D(GraphicsData), .en(demultiplexer_17_out0[11]), .Q(Row14[15:0]), .clk(CLK), .clr(RESET));
  Register #(.width(16)) register_29 (
    .D(GraphicsData), .en(demultiplexer_17_out0[12]), .Q(Row15[31:16]), .clk(CLK), .clr(RESET));
  Register #(.width(16)) register_30 (
    .D(GraphicsData), .en(demultiplexer_17_out0[13]), .Q(Row15[15:0]), .clk(CLK), .clr(RESET));
  Register #(.width(16)) register_31 (
    .D(GraphicsData), .en(demultiplexer_17_out0[14]), .Q(Row16[31:16]), .clk(CLK), .clr(RESET));
  Register #(.width(16)) register_32 (
    .D(GraphicsData), .en(demultiplexer_17_out0[15]), .Q(Row16[15:0]), .clk(CLK), .clr(RESET));
  Demultiplexer #(.disabled(0), .enable("false")) demultiplexer_17 (
    .out0(demultiplexer_17_out0[0]), .out1(demultiplexer_17_out0[1]), .in(demultiplexer_19_out0[8]),
    .sel(CurrReg_q[0]));
  Demultiplexer #(.disabled(0), .enable("false")) demultiplexer_18 (
    .out0(demultiplexer_18_out0[0]), .out1(demultiplexer_18_out0[1]), .in(demultiplexer_19_out16[8]),
    .sel(CurrReg_q[0]));
  Demultiplexer #(.select(5), .disabled(0), .enable("false")) demultiplexer_19 (
    .out0(demultiplexer_19_out0[0]), .out1(demultiplexer_19_out0[1]), .out2(demultiplexer_19_out0[2]),
    .out3(demultiplexer_19_out0[3]), .out4(demultiplexer_19_out0[4]), .out5(demultiplexer_19_out0[5]),
    .out6(demultiplexer_19_out0[6]), .out7(demultiplexer_19_out0[7]), .out8(demultiplexer_19_out0[8]),
    .out9(demultiplexer_19_out0[9]), .out10(demultiplexer_19_out0[10]), .out11(demultiplexer_19_out0[11]),
    .out12(demultiplexer_19_out0[12]), .out13(demultiplexer_19_out0[13]), .out14(demultiplexer_19_out0[14]),
    .out15(demultiplexer_19_out0[15]), .out16(demultiplexer_19_out16[0]), .out17(demultiplexer_19_out16[1]),
    .out18(demultiplexer_19_out16[2]), .out19(demultiplexer_19_out16[3]), .out20(demultiplexer_19_out16[4]),
    .out21(demultiplexer_19_out16[5]), .out22(demultiplexer_19_out16[6]), .out23(demultiplexer_19_out16[7]),
    .out24(demultiplexer_19_out16[8]), .out25(demultiplexer_19_out16[9]), .out26(demultiplexer_19_out16[10]),
    .out27(demultiplexer_19_out16[11]), .out28(demultiplexer_19_out16[12]),
    .out29(demultiplexer_19_out16[13]), .out30(demultiplexer_19_out16[14]),
    .out31(demultiplexer_19_out16[15]), .in(CanReadGraphicsData), .sel(CurrReg_q[5:1]));
  Demultiplexer #(.disabled(0), .enable("false")) demultiplexer_20 (
    .out0(demultiplexer_17_out0[2]), .out1(demultiplexer_17_out0[3]), .in(demultiplexer_19_out0[9]),
    .sel(CurrReg_q[0]));
  Demultiplexer #(.disabled(0), .enable("false")) demultiplexer_21 (
    .out0(demultiplexer_18_out0[2]), .out1(demultiplexer_18_out0[3]), .in(demultiplexer_19_out16[9]),
    .sel(CurrReg_q[0]));
  Demultiplexer #(.disabled(0), .enable("false")) demultiplexer_22 (
    .out0(demultiplexer_17_out0[4]), .out1(demultiplexer_17_out0[5]), .in(demultiplexer_19_out0[10]),
    .sel(CurrReg_q[0]));
  Demultiplexer #(.disabled(0), .enable("false")) demultiplexer_23 (
    .out0(demultiplexer_17_out0[6]), .out1(demultiplexer_17_out0[7]), .in(demultiplexer_19_out0[11]),
    .sel(CurrReg_q[0]));
  Demultiplexer #(.disabled(0), .enable("false")) demultiplexer_24 (
    .out0(demultiplexer_18_out0[4]), .out1(demultiplexer_18_out0[5]), .in(demultiplexer_19_out16[10]),
    .sel(CurrReg_q[0]));
  Demultiplexer #(.disabled(0), .enable("false")) demultiplexer_25 (
    .out0(demultiplexer_18_out0[6]), .out1(demultiplexer_18_out0[7]), .in(demultiplexer_19_out16[11]),
    .sel(CurrReg_q[0]));
  Demultiplexer #(.disabled(0), .enable("false")) demultiplexer_26 (
    .out0(demultiplexer_17_out0[8]), .out1(demultiplexer_17_out0[9]), .in(demultiplexer_19_out0[12]),
    .sel(CurrReg_q[0]));
  Demultiplexer #(.disabled(0), .enable("false")) demultiplexer_27 (
    .out0(demultiplexer_18_out0[8]), .out1(demultiplexer_18_out0[9]), .in(demultiplexer_19_out16[12]),
    .sel(CurrReg_q[0]));
  Register #(.width(16)) register_33 (
    .D(GraphicsData), .en(demultiplexer_2_out0[0]), .Q(Row17[31:16]), .clk(CLK), .clr(RESET));
  Register #(.width(16)) register_34 (
    .D(GraphicsData), .en(demultiplexer_2_out0[1]), .Q(Row17[15:0]), .clk(CLK), .clr(RESET));
  Register #(.width(16)) register_35 (
    .D(GraphicsData), .en(demultiplexer_2_out0[2]), .Q(Row18[31:16]), .clk(CLK), .clr(RESET));
  Register #(.width(16)) register_36 (
    .D(GraphicsData), .en(demultiplexer_2_out0[3]), .Q(Row18[15:0]), .clk(CLK), .clr(RESET));
  Register #(.width(16)) register_37 (
    .D(GraphicsData), .en(demultiplexer_2_out0[4]), .Q(Row19[31:16]), .clk(CLK), .clr(RESET));
  Register #(.width(16)) register_38 (
    .D(GraphicsData), .en(demultiplexer_2_out0[5]), .Q(Row19[15:0]), .clk(CLK), .clr(RESET));
  Register #(.width(16)) register_39 (
    .D(GraphicsData), .en(demultiplexer_2_out0[6]), .Q(Row20[31:16]), .clk(CLK), .clr(RESET));
  Register #(.width(16)) register_40 (
    .D(GraphicsData), .en(demultiplexer_2_out0[7]), .Q(Row20[15:0]), .clk(CLK), .clr(RESET));
  Register #(.width(16)) register_41 (
    .D(GraphicsData), .en(demultiplexer_2_out0[8]), .Q(Row21[31:16]), .clk(CLK), .clr(RESET));
  Register #(.width(16)) register_42 (
    .D(GraphicsData), .en(demultiplexer_2_out0[9]), .Q(Row21[15:0]), .clk(CLK), .clr(RESET));
  Register #(.width(16)) register_43 (
    .D(GraphicsData), .en(demultiplexer_2_out0[10]), .Q(Row22[31:16]), .clk(CLK), .clr(RESET));
  Register #(.width(16)) register_44 (
    .D(GraphicsData), .en(demultiplexer_2_out0[11]), .Q(Row22[15:0]), .clk(CLK), .clr(RESET));
  Register #(.width(16)) register_45 (
    .D(GraphicsData), .en(demultiplexer_2_out0[12]), .Q(Row23[31:16]), .clk(CLK), .clr(RESET));
  Register #(.width(16)) register_46 (
    .D(GraphicsData), .en(demultiplexer_2_out0[13]), .Q(Row23[15:0]), .clk(CLK), .clr(RESET));
  Register #(.width(16)) register_47 (
    .D(GraphicsData), .en(demultiplexer_2_out0[14]), .Q(Row24[31:16]), .clk(CLK), .clr(RESET));
  Register #(.width(16)) register_48 (
    .D(GraphicsData), .en(demultiplexer_2_out0[15]), .Q(Row24[15:0]), .clk(CLK), .clr(RESET));
  Demultiplexer #(.disabled(0), .enable("false")) demultiplexer_28 (
    .out0(demultiplexer_17_out0[10]), .out1(demultiplexer_17_out0[11]), .in(demultiplexer_19_out0[13]),
    .sel(CurrReg_q[0]));
  Demultiplexer #(.disabled(0), .enable("false")) demultiplexer_29 (
    .out0(demultiplexer_18_out0[10]), .out1(demultiplexer_18_out0[11]), .in(demultiplexer_19_out16[13]),
    .sel(CurrReg_q[0]));
  Demultiplexer #(.disabled(0), .enable("false")) demultiplexer_30 (
    .out0(demultiplexer_17_out0[14]), .out1(demultiplexer_17_out0[15]), .in(demultiplexer_19_out0[15]),
    .sel(CurrReg_q[0]));
  Demultiplexer #(.disabled(0), .enable("false")) demultiplexer_31 (
    .out0(demultiplexer_17_out0[12]), .out1(demultiplexer_17_out0[13]), .in(demultiplexer_19_out0[14]),
    .sel(CurrReg_q[0]));
  Demultiplexer #(.disabled(0), .enable("false")) demultiplexer_32 (
    .out0(demultiplexer_18_out0[12]), .out1(demultiplexer_18_out0[13]), .in(demultiplexer_19_out16[14]),
    .sel(CurrReg_q[0]));
  Demultiplexer #(.disabled(0), .enable("false")) demultiplexer_33 (
    .out0(demultiplexer_18_out0[14]), .out1(demultiplexer_18_out0[15]), .in(demultiplexer_19_out16[15]),
    .sel(CurrReg_q[0]));
  Register #(.width(16)) register_49 (
    .D(GraphicsData), .en(demultiplexer_18_out0[0]), .Q(Row25[31:16]), .clk(CLK), .clr(RESET));
  Register #(.width(16)) register_50 (
    .D(GraphicsData), .en(demultiplexer_18_out0[1]), .Q(Row25[15:0]), .clk(CLK), .clr(RESET));
  Register #(.width(16)) register_51 (
    .D(GraphicsData), .en(demultiplexer_18_out0[2]), .Q(Row26[31:16]), .clk(CLK), .clr(RESET));
  Register #(.width(16)) register_52 (
    .D(GraphicsData), .en(demultiplexer_18_out0[3]), .Q(Row26[15:0]), .clk(CLK), .clr(RESET));
  Register #(.width(16)) register_53 (
    .D(GraphicsData), .en(demultiplexer_18_out0[4]), .Q(Row27[31:16]), .clk(CLK), .clr(RESET));
  Register #(.width(16)) register_54 (
    .D(GraphicsData), .en(demultiplexer_18_out0[5]), .Q(Row27[15:0]), .clk(CLK), .clr(RESET));
  Register #(.width(16)) register_55 (
    .D(GraphicsData), .en(demultiplexer_18_out0[6]), .Q(Row28[31:16]), .clk(CLK), .clr(RESET));
  Register #(.width(16)) register_56 (
    .D(GraphicsData), .en(demultiplexer_18_out0[7]), .Q(Row28[15:0]), .clk(CLK), .clr(RESET));
  Register #(.width(16)) register_57 (
    .D(GraphicsData), .en(demultiplexer_18_out0[8]), .Q(Row29[31:16]), .clk(CLK), .clr(RESET));
  Register #(.width(16)) register_58 (
    .D(GraphicsData), .en(demultiplexer_18_out0[9]), .Q(Row29[15:0]), .clk(CLK), .clr(RESET));
  Register #(.width(16)) register_59 (
    .D(GraphicsData), .en(demultiplexer_18_out0[10]), .Q(Row30[31:16]), .clk(CLK), .clr(RESET));
  Register #(.width(16)) register_60 (
    .D(GraphicsData), .en(demultiplexer_18_out0[11]), .Q(Row30[15:0]), .clk(CLK), .clr(RESET));
  Register #(.width(16)) register_61 (
    .D(GraphicsData), .en(demultiplexer_18_out0[12]), .Q(Row31[31:16]), .clk(CLK), .clr(RESET));
  Register #(.width(16)) register_62 (
    .D(GraphicsData), .en(demultiplexer_18_out0[13]), .Q(Row31[15:0]), .clk(CLK), .clr(RESET));
  Register #(.width(16)) register_63 (
    .D(GraphicsData), .en(demultiplexer_18_out0[14]), .Q(Row32[31:16]), .clk(CLK), .clr(RESET));
  Register #(.width(16)) register_64 (
    .D(GraphicsData), .en(demultiplexer_18_out0[15]), .Q(Row32[15:0]), .clk(CLK), .clr(RESET));
endmodule
